# Fritzing sketch circuito ledStrip (saved by Fritzing 0.9.3b)
breadboards: 1

parts:
  WS2812B1 = WS2812B 12V Strip -- White (60/m)
  WS2812B2 = WS2812B 12V Strip -- White (60/m)
  WS2812B3 = WS2812B 12V Strip -- White (60/m)
  WS2812B4 = WS2812B 12V Strip -- White (60/m)
  Componente1 = Arduino Uno (Rev3)
  Q2 = npn-Powertransistor [package="TO220 [THT]"]
  Q1 = npn-Powertransistor [package="TO220 [THT]"]
  Q3 = npn-Powertransistor [package="TO220 [THT]"]
  Q4 = npn-Powertransistor [package="TO220 [THT]"]
  Power_plug1 = Power plug
  R1 = Resistor [tolerance=±5% resistance=330k package=THT]
  R3 = Resistor [tolerance=±5% resistance=330 package=THT]
  R4 = Resistor [tolerance=±5% resistance=330 package=THT]
  R5 = Resistor [tolerance=±5% resistance=330 package=THT]

nets:
  N1: WS2812B1.DI, WS2812B2.DI, WS2812B3.DI, WS2812B4.DI, Power_plug1.VCC
  N2: WS2812B1.GND, Q2.collector
  N3: WS2812B2.GND, Q1.collector
  N4: WS2812B3.GND, Q4.collector
  N5: WS2812B4.GND, Q3.collector
  N6: Componente1.D9_PWM, R4.Pin_0
  N7: Componente1.D11_PWM/MOSI, R3.Pin_0
  N8: Componente1.D5_PWM, R1.Pin_0
  N9: Componente1.D6_PWM, R5.Pin_0
  GND: Componente1.GND, Q2.emitter, Q1.emitter, Q3.emitter, Q4.emitter, Power_plug1.GND
  N10: Q2.base, R1.Pin_1
  N11: Q1.base, R5.Pin_1
  N12: Q3.base, R3.Pin_1
  N13: Q4.base, R4.Pin_1

notes:
  12v
  330R
  Tira LED Blanco
  TIP 120/122
  Amarillo = Q
  Azul = E
  Rojo = C
  Verde = Z

custom parts:
  WS2812B 12V Strip -- White (60/m): WS2812B LED Strip, White, 60 pixels per meter, 12V Power
